// Logisim project initial_labs.circ as structural Verilog: 3 circuits, main circuit x3plus6
module x3plus6 (
  input  A,
  input  B,
  output W,
  output X,
  output Y,
  output Z
);

  wire not_1_out;

  not not_1 (not_1_out, B);
  or or_1 (W, A, B);
  or or_2 (X, A, not_1_out);
  xnor xnor_1 (Y, A, B);

  assign Z = B;

  // Notes on the sheet:
  //   David Ludwig
  //   CLA 01
  //   x3plus6
endmodule

module generator (
  input  [2:0] Input,
  output [3:0] Output
);

  wire xor_1_out;

  xor xor_1 (xor_1_out, Input[1], Input[0]);
  xor xor_2 (Output[3], Input[2], xor_1_out);

  assign Output[2:0] = Input;

  // Notes on the sheet:
  //   David Ludwig
  //   CLA 02
  //   Generator
endmodule

module \checker  (
  input  [3:0] Input,
  output Output
);

  wire xor_1_out, xor_2_out;

  xor xor_1 (xor_1_out, Input[2], Input[3]);
  xor xor_2 (xor_2_out, Input[1], xor_1_out);
  xor xor_3 (Output, Input[0], xor_2_out);

  // Notes on the sheet:
  //   David Ludwig
  //   CLA 02
  //   Checker
endmodule
