// Logisim project custom_reg.circ as structural Verilog: 1 circuit, main circuit 1bit_reg
module _1bit_reg (
  input  Clock,
  input  Data,
  input  Load,
  input  Clear,
  output Data_out
);

  wire and_1_out, and_2_out, not_1_out, not_2_out;

  and and_1 (and_1_out, Data, Load);
  not not_1 (not_1_out, Data);
  and and_2 (and_2_out, not_1_out, Load);
  J_K_Flip_Flop j_k_ff_1 (
    .J(and_1_out), .clk(Clock), .K(and_2_out), .Q(Data_out), .preset(1'b0), .en(not_2_out), .reset(Clear));  // open: Qn
  not not_2 (not_2_out, Clear);

  // Notes on the sheet:
  //   David Ludwig
  //   CLA 5
  //   1bit_reg
endmodule
