// Logisim project RSC.circ as structural Verilog: 6 circuits, main circuit ALU
module ALU (
  input  [31:0] A,
  input  [31:0] B,
  input  S2,
  input  S1,
  input  S0,
  output [31:0] ALU_Out
);

  wire [31:0] arith_u_1_au_out, logic_u_1_logic_out;

  Arith_U arith_u_1 (.A(A), .B(B), .S1(S1), .S0(S0), .AU_Out(arith_u_1_au_out));
  Multiplexer #(.width(32), .enable("false")) multiplexer_1 (
    .in0(arith_u_1_au_out), .in1(logic_u_1_logic_out), .out(ALU_Out), .sel(S2));
  Logic_U logic_u_1 (.A(A), .B(B), .S1(S1), .S0(S0), .Logic_Out(logic_u_1_logic_out));

  // Notes on the sheet:
  //   David Ludwig
  //   CLA 6
  //   ALU
endmodule

// AU
module Arith_U (
  input  [31:0] A,
  input  [31:0] B,
  input  S1,
  input  S0,
  output [31:0] AU_Out
);

  wire and_1_out, xnor_1_out;
  wire [31:0] adder_1_out, multiplexer_1_out, not_1_out;

  assign not_1_out = ~B;  // NOT_Gate not_1, 32 bits wide
  Multiplexer #(.select(2), .width(32), .enable("false")) multiplexer_1 (
    .in0(not_1_out), .in1(B), .in2(32'h1), .out(multiplexer_1_out), .sel({S1, S0}));  // open: in3
  xnor xnor_1 (xnor_1_out, S1, S0);
  Adder #(.width(32)) adder_1 (.a(A), .b(multiplexer_1_out), .out(adder_1_out), .cin(xnor_1_out));  // open: cout
  Multiplexer #(.width(32), .enable("false")) multiplexer_2 (.in0(adder_1_out), .in1(B), .out(AU_Out), .sel(and_1_out));
  and and_1 (and_1_out, S1, S0);

  // Notes on the sheet:
  //   David Ludwig
  //   CLA 6
  //   Arith_U
endmodule

// LU
module Logic_U (
  input  [31:0] A,
  input  [31:0] B,
  input  S1,
  input  S0,
  output [31:0] Logic_Out
);

  wire [31:0] and_1_out, not_1_out, or_1_out, shifter_1_out;

  assign and_1_out = A & B;  // AND_Gate and_1, 32 bits wide
  assign or_1_out = A | B;  // OR_Gate or_1, 32 bits wide
  Shifter #(.width(32), .shift("ar")) shifter_1 (.in(A), .\dist (5'b00001), .out(shifter_1_out));
  assign not_1_out = ~A;  // NOT_Gate not_1, 32 bits wide
  Multiplexer #(.select(2), .width(32), .enable("false")) multiplexer_1 (
    .in0(and_1_out), .in1(or_1_out), .in2(shifter_1_out), .in3(not_1_out), .out(Logic_Out), .sel({S1, S0}));

  // Notes on the sheet:
  //   David Ludwig
  //   CLA 6
  //   Logic_U
endmodule

module SC (
  input  Clock,
  input  Clear,
  output [2:0] SEQ_out
);

  wire [2:0] adder_1_out;

  Adder #(.width(3)) adder_1 (.a(SEQ_out), .b(3'b001), .out(adder_1_out));  // open: cin, cout
  Register #(.width(3)) register_1 (.D(adder_1_out), .en(Clock), .Q(SEQ_out), .clk(Clock), .clr(Clear));

  // Notes on the sheet:
  //   David Ludwig
  //   CLA 7
  //   SC
endmodule

module Decoder (
  input  [31:0] IR_In,
  output [15:0] D_Out,
  output [3:0] Debug_Instruction
);

  wire or_1_out;
  wire [3:0] or_2_out;
  wire [15:0] decoder_1_out0;

  Multiplexer #(.width(16), .enable("false")) multiplexer_1 (
    .in0(decoder_1_out0), .in1({16{1'b0}}), .out(D_Out), .sel(or_1_out));
  or or_1 (or_1_out, or_2_out[0], or_2_out[1], or_2_out[2], or_2_out[3]);
  Decoder_part #(.select(4), .enable("false")) decoder_1 (
    .out0(decoder_1_out0[0]), .out1(decoder_1_out0[1]), .out2(decoder_1_out0[2]), .out3(decoder_1_out0[3]),
    .out4(decoder_1_out0[4]), .out5(decoder_1_out0[5]), .out6(decoder_1_out0[6]), .out7(decoder_1_out0[7]),
    .out8(decoder_1_out0[8]), .out9(decoder_1_out0[9]), .out10(decoder_1_out0[10]),
    .out11(decoder_1_out0[11]), .out12(decoder_1_out0[12]), .out13(decoder_1_out0[13]),
    .out14(decoder_1_out0[14]), .out15(decoder_1_out0[15]), .sel(IR_In[3:0]));
  assign or_2_out = IR_In[7:4] | IR_In[11:8] | IR_In[15:12] | IR_In[19:16] | IR_In[23:20] | IR_In[27:24] | IR_In[31:28];  // OR_Gate or_2, 4 bits wide

  assign Debug_Instruction = IR_In[3:0];
endmodule

module Timer (
  input  Clock,
  input  Stop,
  input  Clear,
  output [7:0] T_Out
);

  wire [2:0] sc_1_seq_out;
  wire [7:0] decoder_1_out0;

  Multiplexer #(.width(8), .enable("false")) multiplexer_1 (
    .in0(decoder_1_out0), .in1({8{1'b0}}), .out(T_Out), .sel(Stop));
  Decoder_part #(.select(3), .enable("false")) decoder_1 (
    .out0(decoder_1_out0[0]), .out1(decoder_1_out0[1]), .out2(decoder_1_out0[2]), .out3(decoder_1_out0[3]),
    .out4(decoder_1_out0[4]), .out5(decoder_1_out0[5]), .out6(decoder_1_out0[6]), .out7(decoder_1_out0[7]),
    .sel(sc_1_seq_out));
  SC sc_1 (.Clock(Clock), .Clear(Clear), .SEQ_out(sc_1_seq_out));
endmodule
