// Logisim project bin_converter.circ as structural Verilog: 2 circuits, main circuit bin_converter
module bin_converter (
  input  [2:0] Input,
  output T,
  output U,
  output V,
  output W,
  output X,
  output Y,
  output Z
);

  wire and_4_out, or_1_out;

  and and_1 (T, Input[0], U);
  and and_2 (U, Input[2], Input[1]);
  and and_3 (V, Input[2], or_1_out);
  or or_1 (or_1_out, Input[1], Input[0]);
  or or_2 (X, Input[2], and_4_out);
  and and_4 (and_4_out, Input[1], Input[0]);
  or or_3 (Y, Input[2], Input[1]);
  or or_4 (Z, Y, Input[0]);

  assign W = Input[2];

  // Notes on the sheet:
  //   David Ludwig
  //   OLA 3
  //   bin_converter
endmodule

module display (
  input  [2:0] in_1
);

  wire bin_converter_1_t, bin_converter_1_u, bin_converter_1_v, bin_converter_1_w, bin_converter_1_x,
       bin_converter_1_y, bin_converter_1_z;

  bin_converter bin_converter_1 (
    .Input(in_1), .T(bin_converter_1_t), .U(bin_converter_1_u), .V(bin_converter_1_v), .W(bin_converter_1_w),
    .X(bin_converter_1_x), .Y(bin_converter_1_y), .Z(bin_converter_1_z));
  LED led_1 (.in(bin_converter_1_t));
  LED led_2 (.in(bin_converter_1_u));
  LED led_3 (.in(bin_converter_1_v));
  LED led_4 (.in(bin_converter_1_w));
  LED led_5 (.in(bin_converter_1_x));
  LED led_6 (.in(bin_converter_1_y));
  LED led_7 (.in(bin_converter_1_z));

  // Notes on the sheet:
  //   David Ludwig
  //   OLA 3
  //   display
endmodule
