// Logisim project mod_counter.circ as structural Verilog: 2 circuits, main circuit Mod9
module Mod9 (
  input  Clock,
  output [3:0] out_2
);

  wire and_1_out, and_2_out, B_qn, nand_1_out, nor_1_out;

  and and_1 (and_1_out, B_qn, out_2[0]);
  nor nor_1 (nor_1_out, out_2[3], out_2[2]);
  and and_2 (and_2_out, and_1_out, out_2[1]);
  nand nand_1 (nand_1_out, out_2[1], out_2[0]);
  J_K_Flip_Flop A (.J(and_2_out), .clk(Clock), .K(1'b1), .Q(out_2[3]));  // open: Qn, preset, en, reset
  J_K_Flip_Flop B (.J(nand_1_out), .clk(Clock), .K(1'b1), .Q(out_2[2]), .Qn(B_qn));  // open: preset, en, reset
  J_K_Flip_Flop C (.J(and_1_out), .clk(Clock), .K(and_1_out), .Q(out_2[1]));  // open: Qn, preset, en, reset
  J_K_Flip_Flop D (.J(nor_1_out), .clk(Clock), .K(and_1_out), .Q(out_2[0]));  // open: Qn, preset, en, reset

  // Notes on the sheet:
  //   David Ludwig
  //   OLA 4
  //   Mod9
endmodule

module Display (
  input  DP
);

  wire Clock_out, n7segdecoder_1_a, n7segdecoder_1_b, n7segdecoder_1_c, n7segdecoder_1_d,
       n7segdecoder_1_dp_out, n7segdecoder_1_e, n7segdecoder_1_f, n7segdecoder_1_g;
  wire [3:0] mod9_1_out_2;

  Clock Clock (.out(Clock_out));
  Mod9 mod9_1 (.Clock(Clock_out), .out_2(mod9_1_out_2));
  _7SegDecoder u_7segdecoder_1 (
    .BCD_In(mod9_1_out_2), .DP_In(DP), .a(n7segdecoder_1_a), .b(n7segdecoder_1_b), .c(n7segdecoder_1_c),
    .d(n7segdecoder_1_d), .e(n7segdecoder_1_e), .f(n7segdecoder_1_f), .g(n7segdecoder_1_g),
    .DP_Out(n7segdecoder_1_dp_out));
  _7_Segment_Display u_7_segment_display_1 (
    .g(n7segdecoder_1_g), .f(n7segdecoder_1_f), .a(n7segdecoder_1_a), .b(n7segdecoder_1_b),
    .e(n7segdecoder_1_e), .d(n7segdecoder_1_d), .c(n7segdecoder_1_c), .dp(n7segdecoder_1_dp_out));

  // Notes on the sheet:
  //   David Ludwig
  //   OLA 4
  //   Display
endmodule
