// Logisim project RSC.circ as structural Verilog: 5 circuits, main circuit ALU
module ALU (
  input  [31:0] A,
  input  [31:0] B,
  input  S2,
  input  S1,
  input  S0,
  output [31:0] ALU_Out
);

  wire [31:0] arith_u_1_au_out, logic_u_1_logic_out;

  Arith_U arith_u_1 (.A(A), .B(B), .S1(S1), .S0(S0), .AU_Out(arith_u_1_au_out));
  Multiplexer #(.width(32), .enable("false")) multiplexer_1 (
    .in0(arith_u_1_au_out), .in1(logic_u_1_logic_out), .out(ALU_Out), .sel(S2));
  Logic_U logic_u_1 (.A(A), .B(B), .S1(S1), .S0(S0), .Logic_Out(logic_u_1_logic_out));

  // Notes on the sheet:
  //   David Ludwig
  //   CLA 6
  //   ALU
endmodule

// AU
module Arith_U (
  input  [31:0] A,
  input  [31:0] B,
  input  S1,
  input  S0,
  output [31:0] AU_Out
);

  wire and_1_out, xnor_1_out;
  wire [31:0] adder_1_out, multiplexer_1_out, not_1_out;

  assign not_1_out = ~B;  // NOT_Gate not_1, 32 bits wide
  Multiplexer #(.select(2), .width(32), .enable("false")) multiplexer_1 (
    .in0(not_1_out), .in1(B), .in2(32'h1), .out(multiplexer_1_out), .sel({S1, S0}));  // open: in3
  xnor xnor_1 (xnor_1_out, S1, S0);
  Adder #(.width(32)) adder_1 (.a(A), .b(multiplexer_1_out), .out(adder_1_out), .cin(xnor_1_out));  // open: cout
  Multiplexer #(.width(32), .enable("false")) multiplexer_2 (.in0(adder_1_out), .in1(B), .out(AU_Out), .sel(and_1_out));
  and and_1 (and_1_out, S1, S0);

  // Notes on the sheet:
  //   David Ludwig
  //   CLA 6
  //   Arith_U
endmodule

// LU
module Logic_U (
  input  [31:0] A,
  input  [31:0] B,
  input  S1,
  input  S0,
  output [31:0] Logic_Out
);

  wire [31:0] and_1_out, not_1_out, or_1_out, shifter_1_out;

  assign and_1_out = A & B;  // AND_Gate and_1, 32 bits wide
  assign or_1_out = A | B;  // OR_Gate or_1, 32 bits wide
  Shifter #(.width(32), .shift("ar")) shifter_1 (.in(A), .\dist (5'b00001), .out(shifter_1_out));
  assign not_1_out = ~A;  // NOT_Gate not_1, 32 bits wide
  Multiplexer #(.select(2), .width(32), .enable("false")) multiplexer_1 (
    .in0(and_1_out), .in1(or_1_out), .in2(shifter_1_out), .in3(not_1_out), .out(Logic_Out), .sel({S1, S0}));

  // Notes on the sheet:
  //   David Ludwig
  //   CLA 6
  //   Logic_U
endmodule

module SC (
  input  Clock,
  input  Clear,
  output [2:0] SEQ_out
);

  wire [2:0] adder_1_out;

  Adder #(.width(3)) adder_1 (.a(SEQ_out), .b(3'b001), .out(adder_1_out));  // open: cin, cout
  Register #(.width(3)) register_1 (.D(adder_1_out), .Q(SEQ_out), .clk(Clock), .clr(Clear));  // open: en

  // Notes on the sheet:
  //   David Ludwig
  //   CLA 7
  //   SC
endmodule

module RSC (
);

  wire Primary_clock_out;
  wire [31:0] acc_1_data_out, alu_1_alu_out, ar_1_data_out, dr_1_data_out, pc_1_bus_out;

  Clock Primary_clock (.out(Primary_clock_out));
  AR ar_1 (.Data_In(pc_1_bus_out), .Clock(Primary_clock_out), .Data_Out(ar_1_data_out));  // open: Load
  R r_1 (.Data_In(pc_1_bus_out), .Clock(Primary_clock_out));  // open: Load, Bus, Data_Out
  ALU alu_1 (.A(acc_1_data_out), .B(pc_1_bus_out), .ALU_Out(alu_1_alu_out));  // open: S2, S1, S0
  PC pc_1 (
    .Data_In(pc_1_bus_out), .Clock(Primary_clock_out), .Bus_Out(pc_1_bus_out));  // open: Count, Load, Bus, Data_Out
  DR dr_1 (.Data_In(pc_1_bus_out), .Clock(Primary_clock_out), .Data_Out(dr_1_data_out));  // open: Load, Bus
  ACC acc_1 (
    .Data_In(alu_1_alu_out), .Clock(Primary_clock_out), .Data_Out(acc_1_data_out), .Bus_Out(pc_1_bus_out));  // open: Load, Clear, Bus
  OUTR outr_1 (.Data_In(pc_1_bus_out), .Clock(Primary_clock_out));  // open: Load, Data_Out
  RAM #(.addrWidth(16), .dataWidth(32)) ram_1 (
    .addr(ar_1_data_out[15:0]), .data(pc_1_bus_out), .clk(Primary_clock_out));  // open: sel, ld, clr
  IR ir_1 (.Data_In(dr_1_data_out), .Clock(Primary_clock_out));  // open: Load, Data_Out

  // Notes on the sheet:
  //   David Ludwig
  //   OLA 6
  //   RSC
endmodule
