// Logisim project RSC.circ as structural Verilog: 9 circuits, main circuit ALU
module ALU (
  input  [31:0] A,
  input  [31:0] B,
  input  S2,
  input  S1,
  input  S0,
  output [31:0] ALU_Out
);

  wire [31:0] arith_u_1_au_out, logic_u_1_logic_out;

  Arith_U arith_u_1 (.A(A), .B(B), .S1(S1), .S0(S0), .AU_Out(arith_u_1_au_out));
  Multiplexer #(.width(32), .enable("false")) multiplexer_1 (
    .in0(arith_u_1_au_out), .in1(logic_u_1_logic_out), .out(ALU_Out), .sel(S2));
  Logic_U logic_u_1 (.A(A), .B(B), .S1(S1), .S0(S0), .Logic_Out(logic_u_1_logic_out));

  // Notes on the sheet:
  //   David Ludwig
  //   CLA 6
  //   ALU
endmodule

// AU
module Arith_U (
  input  [31:0] A,
  input  [31:0] B,
  input  S1,
  input  S0,
  output [31:0] AU_Out
);

  wire and_1_out, xnor_1_out;
  wire [31:0] adder_1_out, multiplexer_1_out, not_1_out;

  assign not_1_out = ~B;  // NOT_Gate not_1, 32 bits wide
  Multiplexer #(.select(2), .width(32), .enable("false")) multiplexer_1 (
    .in0(not_1_out), .in1(B), .in2(32'h1), .out(multiplexer_1_out), .sel({S1, S0}));  // open: in3
  xnor xnor_1 (xnor_1_out, S1, S0);
  Adder #(.width(32)) adder_1 (.a(A), .b(multiplexer_1_out), .out(adder_1_out), .cin(xnor_1_out));  // open: cout
  Multiplexer #(.width(32), .enable("false")) multiplexer_2 (.in0(adder_1_out), .in1(B), .out(AU_Out), .sel(and_1_out));
  and and_1 (and_1_out, S1, S0);

  // Notes on the sheet:
  //   David Ludwig
  //   CLA 6
  //   Arith_U
endmodule

// LU
module Logic_U (
  input  [31:0] A,
  input  [31:0] B,
  input  S1,
  input  S0,
  output [31:0] Logic_Out
);

  wire [31:0] and_1_out, not_1_out, or_1_out, shifter_1_out;

  assign and_1_out = A & B;  // AND_Gate and_1, 32 bits wide
  assign or_1_out = A | B;  // OR_Gate or_1, 32 bits wide
  Shifter #(.width(32), .shift("ar")) shifter_1 (.in(A), .\dist (5'b00001), .out(shifter_1_out));
  assign not_1_out = ~A;  // NOT_Gate not_1, 32 bits wide
  Multiplexer #(.select(2), .width(32), .enable("false")) multiplexer_1 (
    .in0(and_1_out), .in1(or_1_out), .in2(shifter_1_out), .in3(not_1_out), .out(Logic_Out), .sel({S1, S0}));

  // Notes on the sheet:
  //   David Ludwig
  //   CLA 6
  //   Logic_U
endmodule

module Control (
  input  Clock,
  input  [31:0] IR_In,
  input  Z_In,
  output IR_LD,
  output [7:0] T,
  output RAM_R_prime_W,
  output RAM_EN,
  output AR_LD,
  output PC_BUS,
  output PC_INC,
  output PC_LD,
  output R_BUS,
  output R_LD,
  output ACC_BUS,
  output ACC_CLR,
  output ACC_LD,
  output [2:0] ALU_S,
  output OUTR_LD,
  output Z_LD,
  output [3:0] D
);

  wire and_1_out, S_data_out, undriven;
  wire [15:0] decoder_1_d_out;

  Timer timer_1 (.T_Out(T), .Clock(Clock), .Stop(S_data_out));  // open: Clear
  _1bit_reg S (.Data(and_1_out), .Clock(Clock), .Load(undriven), .Clear(1'b0), .Data_out(S_data_out));
  Decoder decoder_1 (.D_Out(decoder_1_d_out), .Debug_Instruction(D), .IR_In(IR_In));
  and and_1 (and_1_out, undriven, 1'b1);
endmodule

module SC (
  input  Clock,
  input  Clear,
  output [2:0] SEQ_out
);

  wire [2:0] adder_1_out;

  Adder #(.width(3)) adder_1 (.a(SEQ_out), .b(3'b001), .out(adder_1_out));  // open: cin, cout
  Register #(.width(3)) register_1 (.D(adder_1_out), .Q(SEQ_out), .clk(Clock), .clr(Clear));  // open: en

  // Notes on the sheet:
  //   David Ludwig
  //   CLA 7
  //   SC
endmodule

// Z
module Z_Reg (
  input  Clock,
  input  [31:0] ACC_in,
  input  Load,
  output Z_out
);

  wire nor_1_out;
  wire [7:0] or_1_out;

  assign or_1_out = ACC_in[7:0] | ACC_in[15:8] | ACC_in[23:16] | ACC_in[31:24];  // OR_Gate or_1, 8 bits wide
  nor nor_1 (nor_1_out, or_1_out[0], or_1_out[1], or_1_out[2], or_1_out[3], or_1_out[4], or_1_out[5], or_1_out[6], or_1_out[7]);
  _1bit_reg u_1bit_reg_1 (.Data(nor_1_out), .Clock(Clock), .Load(Load), .Clear(1'b0), .Data_out(Z_out));
endmodule

module RSC (
);

  wire control_1_acc_bus, control_1_acc_clr, control_1_acc_ld, control_1_ar_ld, control_1_ir_ld,
       control_1_outr_ld, control_1_pc_bus, control_1_pc_inc, control_1_pc_ld, control_1_r_bus,
       control_1_r_ld, control_1_ram_en, control_1_ram_r_prime_w, control_1_z_ld, Primary_clock_out,
       z_reg_1_z_out;
  wire [2:0] control_1_alu_s;
  wire [31:0] acc_1_data_out, alu_1_alu_out, ar_1_data_out, dr_1_data_out, ir_1_data_out, pc_1_bus_out;

  Clock Primary_clock (.out(Primary_clock_out));
  AR ar_1 (.Data_In(pc_1_bus_out), .Clock(Primary_clock_out), .Load(control_1_ar_ld), .Data_Out(ar_1_data_out));
  R r_1 (
    .Data_In(pc_1_bus_out), .Clock(Primary_clock_out), .Load(control_1_r_ld), .Bus(control_1_r_bus));  // open: Data_Out
  ALU alu_1 (
    .A(acc_1_data_out), .B(pc_1_bus_out), .S2(control_1_alu_s[2]), .S1(control_1_alu_s[1]),
    .S0(control_1_alu_s[0]), .ALU_Out(alu_1_alu_out));
  PC pc_1 (
    .Data_In(pc_1_bus_out), .Clock(Primary_clock_out), .Count(control_1_pc_ld), .Load(control_1_pc_inc),
    .Bus(control_1_pc_bus), .Bus_Out(pc_1_bus_out));  // open: Data_Out
  DR dr_1 (.Data_In(pc_1_bus_out), .Clock(Primary_clock_out), .Data_Out(dr_1_data_out));  // open: Load, Bus
  ACC acc_1 (
    .Data_In(alu_1_alu_out), .Clock(Primary_clock_out), .Load(control_1_acc_ld), .Clear(control_1_acc_clr),
    .Bus(control_1_acc_bus), .Data_Out(acc_1_data_out), .Bus_Out(pc_1_bus_out));
  OUTR outr_1 (.Data_In(pc_1_bus_out), .Clock(Primary_clock_out), .Load(control_1_outr_ld));  // open: Data_Out
  RAM #(.addrWidth(16), .dataWidth(32)) ram_1 (
    .addr(ar_1_data_out[15:0]), .data(pc_1_bus_out), .sel(control_1_ram_en), .clk(Primary_clock_out),
    .ld(control_1_ram_r_prime_w));  // open: clr
  Z_Reg z_reg_1 (.ACC_in(acc_1_data_out), .Clock(Primary_clock_out), .Load(control_1_z_ld), .Z_out(z_reg_1_z_out));
  IR ir_1 (.Data_In(dr_1_data_out), .Clock(Primary_clock_out), .Load(control_1_ir_ld), .Data_Out(ir_1_data_out));
  Control control_1 (
    .RAM_R_prime_W(control_1_ram_r_prime_w), .RAM_EN(control_1_ram_en), .AR_LD(control_1_ar_ld),
    .PC_BUS(control_1_pc_bus), .PC_INC(control_1_pc_inc), .PC_LD(control_1_pc_ld), .R_BUS(control_1_r_bus),
    .R_LD(control_1_r_ld), .ACC_BUS(control_1_acc_bus), .ACC_CLR(control_1_acc_clr),
    .ACC_LD(control_1_acc_ld), .ALU_S(control_1_alu_s), .OUTR_LD(control_1_outr_ld), .Z_LD(control_1_z_ld),
    .IR_LD(control_1_ir_ld), .Clock(Primary_clock_out), .Z_In(z_reg_1_z_out), .IR_In(ir_1_data_out));  // open: T, D

  // Notes on the sheet:
  //   David Ludwig
  //   OLA 6
  //   RSC
endmodule

module Decoder (
  input  [31:0] IR_In,
  output [15:0] D_Out,
  output [3:0] Debug_Instruction
);

  wire or_1_out;
  wire [3:0] or_2_out;
  wire [15:0] decoder_1_out0;

  Multiplexer #(.width(16), .enable("false")) multiplexer_1 (
    .in0(decoder_1_out0), .in1({16{1'b0}}), .out(D_Out), .sel(or_1_out));
  or or_1 (or_1_out, or_2_out[0], or_2_out[1], or_2_out[2], or_2_out[3]);
  Decoder_part #(.select(4), .enable("false")) decoder_1 (
    .out0(decoder_1_out0[0]), .out1(decoder_1_out0[1]), .out2(decoder_1_out0[2]), .out3(decoder_1_out0[3]),
    .out4(decoder_1_out0[4]), .out5(decoder_1_out0[5]), .out6(decoder_1_out0[6]), .out7(decoder_1_out0[7]),
    .out8(decoder_1_out0[8]), .out9(decoder_1_out0[9]), .out10(decoder_1_out0[10]),
    .out11(decoder_1_out0[11]), .out12(decoder_1_out0[12]), .out13(decoder_1_out0[13]),
    .out14(decoder_1_out0[14]), .out15(decoder_1_out0[15]), .sel(IR_In[3:0]));
  assign or_2_out = IR_In[7:4] | IR_In[11:8] | IR_In[15:12] | IR_In[19:16] | IR_In[23:20] | IR_In[27:24] | IR_In[31:28];  // OR_Gate or_2, 4 bits wide

  assign Debug_Instruction = IR_In[3:0];
endmodule

module Timer (
  input  Clock,
  input  Stop,
  input  Clear,
  output [7:0] T_Out
);

  wire [2:0] sc_1_seq_out;
  wire [7:0] decoder_1_out0;

  Multiplexer #(.width(8), .enable("false")) multiplexer_1 (
    .in0(decoder_1_out0), .in1({8{1'b0}}), .out(T_Out), .sel(Stop));
  Decoder_part #(.select(3), .enable("false")) decoder_1 (
    .out0(decoder_1_out0[0]), .out1(decoder_1_out0[1]), .out2(decoder_1_out0[2]), .out3(decoder_1_out0[3]),
    .out4(decoder_1_out0[4]), .out5(decoder_1_out0[5]), .out6(decoder_1_out0[6]), .out7(decoder_1_out0[7]),
    .sel(sc_1_seq_out));
  SC sc_1 (.Clock(Clock), .Clear(Clear), .SEQ_out(sc_1_seq_out));
endmodule
